# Fritzing sketch lpc1114 (saved by Fritzing 0.9.3b)
breadboards: 1

parts:
  J1 = female pin header, 6 pins [form="♀ (female)"]
  U1 = Voltage Regulator - 3.3V [package="TO220 [THT]"]
  S1 = Pushbutton [package="[THT]"]
  IC1 = IC, DIP package, 28 pins
  R2 = Resistor [tolerance=±5% resistance=10 package=THT]
  J2 = female pin header, 6 pins [form="♀ (female)"]
  J3 = female pin header, 6 pins [form="♀ (female)"]
  J4 = female pin header, 4 pins [form="♀ (female)"]
  J5 = female pin header, 6 pins [form="♀ (female)"]
  C1 = Ceramic Capacitor [capacitance=100nF package="100 mil [THT, multilayer]"]
  J6 = female pin header, 2 pins [form="♀ (female)"]
  R3 = Resistor [tolerance=±5% resistance=10k package=THT]

nets:
  N1: J1.pin1, U1.input_voltage, S1.Pin_3, S1.Pin_4, IC1.pin8, IC1.pin22, C1.1, J6.pin1, R3.Pin_1
  N2: J1.pin3, U1.output_voltage
  N3: J1.pin4, IC1.pin15
  N4: J1.pin5, IC1.pin16
  N5: U1.GND, IC1.pin7, IC1.pin21, R2.Pin_1, C1.0, J6.pin2
  N6: S1.Pin_1, S1.Pin_2, IC1.pin23, R2.Pin_0, J5.pin1
  N7: IC1.pin1, J3.pin6
  N8: IC1.pin2, J3.pin5
  N9: IC1.pin3, J3.pin4
  N10: IC1.pin4, J3.pin3
  N11: IC1.pin5, J3.pin2
  N12: IC1.pin6, J3.pin1
  N13: IC1.pin9, J2.pin6
  N14: IC1.pin10, J2.pin5
  N15: IC1.pin11, J2.pin4
  N16: IC1.pin12, J2.pin3
  N17: IC1.pin13, J2.pin2
  N18: IC1.pin14, J2.pin1
  N19: IC1.pin17, J4.pin1
  N20: IC1.pin18, J4.pin2
  N21: IC1.pin19, J4.pin3
  N22: IC1.pin20, J4.pin4
  N23: IC1.pin24, J5.pin2
  N24: IC1.pin25, J5.pin3
  N25: IC1.pin26, J5.pin4
  N26: IC1.pin27, J5.pin5
  N27: IC1.pin28, J5.pin6, R3.Pin_0

notes:
  LPC1114
  GND
  3.3 V
  5 V in
  reset
