# Fritzing sketch lpc1114 (saved by Fritzing 0.9.3b)
breadboards: 1

parts:
  IC1 = IC, DIP package, 28 pins [chip_label=IC]  # not connected
  J1 = female pin header, 6 pins [form="♀ (female)"]
  U1 = Voltage Regulator - 3.3V [package="TO220 [THT]"]
  S1 = Pushbutton [package="[THT]"]
  J2 = male pin header, 2 pins [form="♂ (male)"]

nets:
  N1: J1.pin1, U1.GND, S1.Pin_3, S1.Pin_4, J2.pin1
  N2: J1.pin3, U1.input_voltage
  N3: S1.Pin_1, S1.Pin_2

notes:
  GND
